// Logisim project BFPU.circ as structural Verilog: 1 circuit, main circuit main
module main (
);

  wire and_1_out, and_7_out, and_8_out, BUG_PROG, cells, CLK, JMP, LEND, load, multiplexer_2_out, nor_1_out,
       nor_2_out, not_1_out, not_2_out, not_3_out, not_4_out, not_5_out, not_6_out, not_7_out, not_9_out,
       not_10_out, or_2_out, or_5_out, or_6_out, RST, SAVE, SKIP, SRV, SVE;
  wire [1:0] nor_3_out, or_3_out;
  wire [3:0] H, L, rom_1_data;
  wire [7:0] adder_1_out, adder_2_out, IP_q, multiplexer_1_out, multiplexer_3_out, multiplexer_5_out,
       ram_1_dout, ram_2_dout, register_1_q, subtractor_1_out;
  wire [14:0] adder_3_out, multiplexer_4_out, register_2_q, subtractor_2_out;

  Adder adder_1 (.a(IP_q), .b(8'h1), .out(adder_1_out));  // open: cin, cout
  ROM #(.dataWidth(4)) rom_1 (.addr(IP_q), .data(rom_1_data));
  Register register_1 (.D(register_1_q), .clk(CLK), .Q(register_1_q));  // open: en, clr
  Multiplexer #(.select(2), .width(8)) multiplexer_1 (
    .in0(adder_1_out), .in1(ram_1_dout), .in2({8{1'b0}}), .in3({8{1'b0}}), .out(multiplexer_1_out),
    .sel({RST, JMP}));
  Register IP (.D(multiplexer_1_out), .en(1'b1), .clk(CLK), .Q(IP_q));  // open: clr
  Clock clock_1 (.out(CLK));
  Button u_RST (.out(RST));
  RAM ram_1 (.addr(register_1_q), .we(SAVE), .oe(1'b1), .clk(CLK), .din(IP_q), .dout(ram_1_dout));
  or or_1 (BUG_PROG, IP_q[7], IP_q[6], IP_q[5], IP_q[4], IP_q[3], IP_q[2], IP_q[1], IP_q[0]);
  Hex_Digit_Display hex_digit_display_1 (.value(H));  // open: dp
  Hex_Digit_Display hex_digit_display_2 (.value(L));  // open: dp
  not not_1 (not_1_out, rom_1_data[0]);
  and and_1 (and_1_out, not_1_out, rom_1_data[1], rom_1_data[2]);
  and and_2 (SAVE, and_1_out, SRV);
  not not_2 (not_2_out, SRV);
  Register #(.width(1)) u_Skip (.D(multiplexer_2_out), .en(or_2_out), .clk(CLK), .Q(SKIP));  // open: clr
  Multiplexer multiplexer_2 (.in0(1'b0), .in1(1'b1), .out(multiplexer_2_out));  // open: sel
  or or_2 (or_2_out, SVE, LEND);
  and and_3 (JMP, SRV, rom_1_data[0], rom_1_data[1], rom_1_data[2]);
  and and_4 (SVE, not_2_out, and_1_out);
  and and_5 (LEND, rom_1_data[0], rom_1_data[1], rom_1_data[2]);
  not not_3 (not_3_out, rom_1_data[1]);
  and and_6 (load, rom_1_data[2], not_3_out, rom_1_data[0]);
  not not_4 (not_4_out, rom_1_data[2]);
  not not_5 (not_5_out, rom_1_data[0]);
  not not_6 (not_6_out, rom_1_data[2]);
  not not_7 (not_7_out, rom_1_data[1]);
  nor nor_1 (nor_1_out, rom_1_data[0], not_7_out, rom_1_data[2]);
  and and_7 (and_7_out, rom_1_data[0], rom_1_data[1], not_4_out);
  nor nor_2 (nor_2_out, rom_1_data[0], rom_1_data[1], not_6_out);
  nor nor_3 (nor_3_out[0], rom_1_data[0], rom_1_data[1], rom_1_data[2]);
  nor nor_4 (nor_3_out[1], not_5_out, rom_1_data[1], rom_1_data[2]);
  or or_3 (or_3_out[0], nor_1_out, nor_2_out);
  or or_4 (or_3_out[1], and_7_out, nor_2_out);
  Adder adder_2 (.a(multiplexer_5_out), .b(8'h1), .out(adder_2_out));  // open: cin, cout
  Subtractor subtractor_1 (.a(multiplexer_5_out), .b(8'h1), .out(subtractor_1_out));  // open: bin, bout
  or or_5 (or_5_out, nor_3_out[0], nor_3_out[1]);
  Adder #(.width(15)) adder_3 (.a(register_2_q), .b(15'h1), .out(adder_3_out));  // open: cin, cout
  Subtractor #(.width(15)) subtractor_2 (.a(register_2_q), .b(15'h1), .out(subtractor_2_out));  // open: bin, bout
  Multiplexer #(.select(2), .width(8)) multiplexer_3 (
    .in0(multiplexer_5_out), .in1(adder_2_out), .in2(subtractor_1_out), .in3(8'h8), .out(multiplexer_3_out),
    .sel(or_3_out));
  not not_8 (cells, or_5_out);
  Multiplexer #(.select(2), .width(15)) multiplexer_4 (
    .in0(register_2_q), .in1(adder_3_out), .in2(subtractor_2_out), .out(multiplexer_4_out), .sel(nor_3_out));  // open: in3
  not not_9 (not_9_out, SKIP);
  and and_8 (and_8_out, not_9_out, cells);
  not not_10 (not_10_out, SKIP);
  RAM #(.addrWidth(15), .asyncread("true")) ram_2 (
    .addr(register_2_q), .we(and_8_out), .oe(1'b1), .clk(CLK), .din(multiplexer_3_out), .dout(ram_2_dout));
  Register #(.width(15)) register_2 (.D(multiplexer_4_out), .en(not_10_out), .clk(CLK), .Q(register_2_q));  // open: clr
  Multiplexer #(.width(8)) multiplexer_5 (.in0({8{1'b0}}), .in1(ram_2_dout), .out(multiplexer_5_out), .sel(or_6_out));
  or or_6 (or_6_out, BUG_PROG, JMP);
  Register register_3 (.D(ram_2_dout), .en(load), .clk(CLK), .Q({H, L}));  // open: clr
  or or_7 (SRV, multiplexer_5_out[0], multiplexer_5_out[1], multiplexer_5_out[2], multiplexer_5_out[3], multiplexer_5_out[4], multiplexer_5_out[5], multiplexer_5_out[6], multiplexer_5_out[7]);

  // Notes on the sheet:
  //   contents of rom_1 (hex, n*v repeats v):
  //   4 6 0 2 2 0 2 1 1 3 7 0 0 6 1 1 2 0 0 3 7 1 1 0 5 6 7
  //   Programmspeicher
  //   I/O Anschlüsse
  //   Procssor clock
  //   RESET
  //   Branch
  //   Write enable: BUG; implement Skip
  //   Eingabevektor
  //   Ausgabevektor
  //   Decoder
  //   . / set
  //   > / ptr++
  //   < / ptr--
  //   ALU
  //   + / cell[ptr]++
  //   - / cell[ptr]--
  //   Brainfuck Logik
  //   pointer register
  //   Zellenblock
  //   hässlicher Bugfix
endmodule
